// Logisim project Numeros Primos.circ as structural Verilog
module SHOW_1 (
  input  a,
  input  b,
  input  c,
  input  d,
  input  e,
  output x
);

  wire and_1_out, and_2_out;

  and and_1 (and_1_out, a, c);
  and and_2 (and_2_out, a, b);
  or or_1 (x, and_1_out, and_2_out);
endmodule

module _0_A (
  input  a,
  input  b,
  input  c,
  input  d,
  input  e,
  output x
);

  wire and_1_out, and_2_out, and_3_out, and_4_out, not_1_out, not_2_out, not_3_out, not_4_out, not_5_out,
       not_6_out;

  not not_1 (not_1_out, a);
  not not_2 (not_2_out, b);
  not not_3 (not_3_out, a);
  not not_4 (not_4_out, c);
  not not_5 (not_5_out, d);
  not not_6 (not_6_out, b);
  and and_1 (and_1_out, not_1_out, not_2_out);
  and and_2 (and_2_out, not_3_out, not_4_out, not_5_out);
  and and_3 (and_3_out, not_6_out, c);
  and and_4 (and_4_out, a, b);
  or or_1 (x, and_1_out, and_2_out, and_3_out, and_4_out);
endmodule

module _1_B (
  input  a,
  input  b,
  input  c,
  input  d,
  input  e,
  output x
);


  assign x = 1'b1;
endmodule

module _2_C (
  input  a,
  input  b,
  input  c,
  input  d,
  input  e,
  output x
);

  wire and_1_out, and_2_out, not_1_out, not_2_out, not_3_out;

  not not_1 (not_1_out, b);
  not not_2 (not_2_out, c);
  not not_3 (not_3_out, a);
  and and_1 (and_1_out, not_1_out, not_2_out);
  and and_2 (and_2_out, b, c, d);
  or or_1 (x, not_3_out, and_1_out, and_2_out);
endmodule

module _3_D (
  input  a,
  input  b,
  input  c,
  input  d,
  input  e,
  output x
);

  wire and_1_out, and_2_out, and_3_out, and_4_out, not_1_out, not_2_out, not_3_out, not_4_out, not_5_out,
       not_6_out;

  not not_1 (not_1_out, a);
  not not_2 (not_2_out, b);
  not not_3 (not_3_out, a);
  not not_4 (not_4_out, c);
  not not_5 (not_5_out, d);
  not not_6 (not_6_out, b);
  and and_1 (and_1_out, not_1_out, not_2_out);
  and and_2 (and_2_out, not_3_out, not_4_out, not_5_out);
  and and_3 (and_3_out, not_6_out, c);
  and and_4 (and_4_out, a, b);
  or or_1 (x, and_1_out, and_2_out, and_3_out, and_4_out);
endmodule

module _4_E (
  input  a,
  input  b,
  input  c,
  input  d,
  input  e,
  output x
);

  wire and_1_out, and_2_out, and_3_out, and_4_out, and_5_out, not_1_out, not_2_out, not_3_out, not_4_out,
       not_5_out, not_6_out, not_7_out, not_8_out;

  not not_1 (not_1_out, a);
  not not_2 (not_2_out, b);
  not not_3 (not_3_out, a);
  not not_4 (not_4_out, c);
  not not_5 (not_5_out, d);
  not not_6 (not_6_out, b);
  not not_7 (not_7_out, c);
  not not_8 (not_8_out, d);
  and and_1 (and_1_out, not_1_out, not_2_out);
  and and_2 (and_2_out, not_3_out, not_4_out, not_5_out);
  and and_3 (and_3_out, not_6_out, c);
  and and_4 (and_4_out, a, b, not_7_out);
  and and_5 (and_5_out, a, b, not_8_out);
  or or_1 (x, and_1_out, and_2_out, and_3_out, and_4_out, and_5_out);
endmodule

module _5_F (
  input  a,
  input  b,
  input  c,
  input  d,
  input  e,
  output x
);

  wire and_1_out, and_2_out, not_1_out, not_2_out, not_3_out, not_4_out, not_5_out;

  not not_1 (not_1_out, a);
  not not_2 (not_2_out, b);
  not not_3 (not_3_out, a);
  not not_4 (not_4_out, c);
  not not_5 (not_5_out, d);
  and and_1 (and_1_out, not_1_out, not_2_out);
  and and_2 (and_2_out, not_3_out, not_4_out, not_5_out);
  or or_1 (x, and_1_out, and_2_out);
endmodule

module _6_G (
  input  a,
  input  b,
  input  c,
  input  d,
  input  e,
  output x
);

  wire and_1_out, and_2_out;

  and and_1 (and_1_out, a, c);
  and and_2 (and_2_out, a, b);
  or or_1 (x, and_1_out, and_2_out);
endmodule

module _0__a (
  input  a,
  input  b,
  input  c,
  input  d,
  input  e,
  output x
);

  wire and_1_out, and_2_out, and_3_out, and_4_out, and_5_out, and_6_out, and_7_out, and_8_out, not_1_out,
       not_2_out, not_3_out, not_4_out, not_5_out, not_6_out, not_7_out, not_8_out, not_9_out, not_10_out,
       not_11_out, not_12_out;

  not not_1 (not_1_out, a);
  not not_2 (not_2_out, c);
  not not_3 (not_3_out, e);
  not not_4 (not_4_out, b);
  not not_5 (not_5_out, a);
  not not_6 (not_6_out, a);
  not not_7 (not_7_out, d);
  not not_8 (not_8_out, d);
  not not_9 (not_9_out, b);
  not not_10 (not_10_out, e);
  not not_11 (not_11_out, c);
  not not_12 (not_12_out, e);
  and and_1 (and_1_out, not_1_out, not_2_out, not_3_out);
  and and_2 (and_2_out, not_4_out, d);
  and and_3 (and_3_out, not_5_out, c, e);
  and and_4 (and_4_out, not_6_out, b, not_7_out);
  and and_5 (and_5_out, b, c, not_8_out);
  and and_6 (and_6_out, a, not_9_out, not_10_out);
  and and_7 (and_7_out, a, not_11_out, e);
  and and_8 (and_8_out, a, d, not_12_out);
  or or_1 (x, and_1_out, and_2_out, and_3_out, and_4_out, and_5_out, and_6_out, and_7_out, and_8_out);
endmodule

module _1__b (
  input  a,
  input  b,
  input  c,
  input  d,
  input  e,
  output x
);

  wire and_1_out, and_2_out, and_3_out, and_4_out, and_5_out, and_6_out, and_7_out, and_8_out, and_9_out,
       and_10_out, and_11_out, not_1_out, not_2_out, not_3_out, not_4_out, not_5_out, not_6_out, not_7_out,
       not_8_out, not_9_out, not_10_out, not_11_out, not_12_out, not_13_out, not_14_out, not_15_out,
       not_16_out, not_17_out, not_18_out, not_19_out, not_20_out;

  not not_1 (not_1_out, a);
  not not_2 (not_2_out, c);
  not not_3 (not_3_out, e);
  not not_4 (not_4_out, a);
  not not_5 (not_5_out, d);
  not not_6 (not_6_out, e);
  not not_7 (not_7_out, b);
  not not_8 (not_8_out, c);
  not not_9 (not_9_out, b);
  not not_10 (not_10_out, a);
  not not_11 (not_11_out, d);
  not not_12 (not_12_out, a);
  not not_13 (not_13_out, e);
  not not_14 (not_14_out, d);
  not not_15 (not_15_out, e);
  not not_16 (not_16_out, d);
  not not_17 (not_17_out, b);
  not not_18 (not_18_out, c);
  not not_19 (not_19_out, c);
  not not_20 (not_20_out, e);
  and and_1 (and_1_out, not_1_out, not_2_out, not_3_out);
  and and_2 (and_2_out, not_4_out, not_5_out, not_6_out);
  and and_3 (and_3_out, not_7_out, not_8_out, d);
  and and_4 (and_4_out, not_9_out, d, e);
  and and_5 (and_5_out, not_10_out, b, not_11_out);
  and and_6 (and_6_out, not_12_out, b, not_13_out);
  and and_7 (and_7_out, b, not_14_out, not_15_out);
  and and_8 (and_8_out, b, c, not_16_out);
  and and_9 (and_9_out, a, not_17_out, not_18_out, e);
  and and_10 (and_10_out, a, not_19_out, d, e);
  and and_11 (and_11_out, a, c, not_20_out);
  or or_1 (x, and_1_out, and_2_out, and_3_out, and_4_out, and_5_out, and_6_out, and_7_out, and_8_out, and_9_out, and_10_out, and_11_out);
endmodule

module _2__c (
  input  a,
  input  b,
  input  c,
  input  d,
  input  e,
  output x
);

  wire and_1_out, and_2_out, and_3_out, and_4_out, and_5_out, and_6_out, and_7_out, and_8_out, and_9_out,
       not_1_out, not_2_out, not_3_out, not_4_out, not_5_out, not_6_out, not_7_out, not_8_out, not_9_out,
       not_10_out, not_11_out, not_12_out, not_13_out, not_14_out, not_15_out;

  not not_1 (not_1_out, b);
  not not_2 (not_2_out, d);
  not not_3 (not_3_out, e);
  not not_4 (not_4_out, c);
  not not_5 (not_5_out, d);
  not not_6 (not_6_out, e);
  not not_7 (not_7_out, b);
  not not_8 (not_8_out, a);
  not not_9 (not_9_out, b);
  not not_10 (not_10_out, a);
  not not_11 (not_11_out, d);
  not not_12 (not_12_out, e);
  not not_13 (not_13_out, c);
  not not_14 (not_14_out, d);
  not not_15 (not_15_out, e);
  and and_1 (and_1_out, not_1_out, not_2_out, not_3_out);
  and and_2 (and_2_out, not_4_out, not_5_out, not_6_out);
  and and_3 (and_3_out, not_7_out, d, e);
  and and_4 (and_4_out, not_8_out, not_9_out, c);
  and and_5 (and_5_out, not_10_out, c, d);
  and and_6 (and_6_out, b, not_11_out, e);
  and and_7 (and_7_out, b, d, not_12_out);
  and and_8 (and_8_out, a, not_13_out);
  and and_9 (and_9_out, a, not_14_out, not_15_out);
  or or_1 (x, and_1_out, and_2_out, and_3_out, and_4_out, and_5_out, and_6_out, and_7_out, and_8_out, and_9_out);
endmodule

module _3__d (
  input  a,
  input  b,
  input  c,
  input  d,
  input  e,
  output x
);

  wire and_1_out, and_2_out, and_3_out, and_4_out, and_5_out, and_6_out, and_7_out, and_8_out, and_9_out,
       and_10_out, and_11_out, not_1_out, not_2_out, not_3_out, not_4_out, not_5_out, not_6_out, not_7_out,
       not_8_out, not_9_out, not_10_out, not_11_out, not_12_out, not_13_out, not_14_out, not_15_out,
       not_16_out, not_17_out, not_18_out, not_19_out, not_20_out;

  not not_1 (not_1_out, a);
  not not_2 (not_2_out, c);
  not not_3 (not_3_out, e);
  not not_4 (not_4_out, b);
  not not_5 (not_5_out, c);
  not not_6 (not_6_out, e);
  not not_7 (not_7_out, b);
  not not_8 (not_8_out, c);
  not not_9 (not_9_out, b);
  not not_10 (not_10_out, e);
  not not_11 (not_11_out, c);
  not not_12 (not_12_out, e);
  not not_13 (not_13_out, a);
  not not_14 (not_14_out, d);
  not not_15 (not_15_out, a);
  not not_16 (not_16_out, d);
  not not_17 (not_17_out, d);
  not not_18 (not_18_out, a);
  not not_19 (not_19_out, b);
  not not_20 (not_20_out, e);
  and and_1 (and_1_out, not_1_out, not_2_out, not_3_out);
  and and_2 (and_2_out, not_4_out, not_5_out, not_6_out);
  and and_3 (and_3_out, not_7_out, not_8_out, d);
  and and_4 (and_4_out, not_9_out, d, not_10_out);
  and and_5 (and_5_out, not_11_out, d, not_12_out);
  and and_6 (and_6_out, not_13_out, c, not_14_out, e);
  and and_7 (and_7_out, not_15_out, b, not_16_out);
  and and_8 (and_8_out, b, not_17_out, e);
  and and_9 (and_9_out, not_18_out, b, c, e);
  and and_10 (and_10_out, a, not_19_out, d);
  and and_11 (and_11_out, a, c, not_20_out);
  or or_1 (x, and_1_out, and_2_out, and_3_out, and_4_out, and_5_out, and_6_out, and_7_out, and_8_out, and_9_out, and_10_out, and_11_out);
endmodule

module _4__e (
  input  a,
  input  b,
  input  c,
  input  d,
  input  e,
  output x
);

  wire and_1_out, and_2_out, and_3_out, and_4_out, and_5_out, and_6_out, and_7_out, and_8_out, and_9_out,
       not_1_out, not_2_out, not_3_out, not_4_out, not_5_out, not_6_out, not_7_out, not_8_out, not_9_out,
       not_10_out, not_11_out, not_12_out, not_13_out, not_14_out, not_15_out, not_16_out, not_17_out,
       not_18_out, not_19_out;

  not not_1 (not_1_out, a);
  not not_2 (not_2_out, b);
  not not_3 (not_3_out, c);
  not not_4 (not_4_out, d);
  not not_5 (not_5_out, b);
  not not_6 (not_6_out, c);
  not not_7 (not_7_out, e);
  not not_8 (not_8_out, b);
  not not_9 (not_9_out, e);
  not not_10 (not_10_out, c);
  not not_11 (not_11_out, e);
  not not_12 (not_12_out, a);
  not not_13 (not_13_out, d);
  not not_14 (not_14_out, e);
  not not_15 (not_15_out, a);
  not not_16 (not_16_out, c);
  not not_17 (not_17_out, b);
  not not_18 (not_18_out, d);
  not not_19 (not_19_out, e);
  and and_1 (and_1_out, not_1_out, not_2_out, not_3_out, not_4_out);
  and and_2 (and_2_out, not_5_out, not_6_out, not_7_out);
  and and_3 (and_3_out, not_8_out, d, not_9_out);
  and and_4 (and_4_out, not_10_out, d, not_11_out);
  and and_5 (and_5_out, not_12_out, b, not_13_out, not_14_out);
  and and_6 (and_6_out, not_15_out, b, not_16_out, d);
  and and_7 (and_7_out, a, not_17_out, c, not_18_out);
  and and_8 (and_8_out, a, c, not_19_out);
  and and_9 (and_9_out, a, b, c, d);
  or or_1 (x, and_1_out, and_2_out, and_3_out, and_4_out, and_5_out, and_6_out, and_7_out, and_8_out, and_9_out);
endmodule

module _5__f (
  input  a,
  input  b,
  input  c,
  input  d,
  input  e,
  output x
);

  wire and_1_out, and_2_out, and_3_out, and_4_out, and_5_out, and_6_out, and_7_out, and_8_out, and_9_out,
       not_1_out, not_2_out, not_3_out, not_4_out, not_5_out, not_6_out, not_7_out, not_8_out, not_9_out,
       not_10_out, not_11_out, not_12_out, not_13_out, not_14_out, not_15_out, not_16_out, not_17_out;

  not not_1 (not_1_out, a);
  not not_2 (not_2_out, b);
  not not_3 (not_3_out, d);
  not not_4 (not_4_out, a);
  not not_5 (not_5_out, b);
  not not_6 (not_6_out, e);
  not not_7 (not_7_out, b);
  not not_8 (not_8_out, d);
  not not_9 (not_9_out, a);
  not not_10 (not_10_out, c);
  not not_11 (not_11_out, c);
  not not_12 (not_12_out, e);
  not not_13 (not_13_out, d);
  not not_14 (not_14_out, e);
  not not_15 (not_15_out, b);
  not not_16 (not_16_out, c);
  not not_17 (not_17_out, d);
  and and_1 (and_1_out, not_1_out, not_2_out, not_3_out);
  and and_2 (and_2_out, not_4_out, not_5_out, c, not_6_out);
  and and_3 (and_3_out, not_7_out, c, not_8_out);
  and and_4 (and_4_out, not_9_out, b, not_10_out);
  and and_5 (and_5_out, b, c, d);
  and and_6 (and_6_out, a, not_11_out, not_12_out);
  and and_7 (and_7_out, a, not_13_out, not_14_out);
  and and_8 (and_8_out, a, not_15_out, not_16_out, d);
  and and_9 (and_9_out, a, b, not_17_out);
  or or_1 (x, and_1_out, and_2_out, and_3_out, and_4_out, and_5_out, and_6_out, and_7_out, and_8_out, and_9_out);
endmodule

module _6__g (
  input  a,
  input  b,
  input  c,
  input  d,
  input  e,
  output x
);

  wire and_1_out, and_2_out, and_3_out, and_4_out, and_5_out, and_6_out, and_7_out, not_1_out, not_2_out,
       not_3_out, not_4_out, not_5_out, not_6_out, not_7_out, not_8_out, not_9_out, not_10_out, not_11_out;

  not not_1 (not_1_out, b);
  not not_2 (not_2_out, c);
  not not_3 (not_3_out, b);
  not not_4 (not_4_out, e);
  not not_5 (not_5_out, a);
  not not_6 (not_6_out, d);
  not not_7 (not_7_out, d);
  not not_8 (not_8_out, a);
  not not_9 (not_9_out, c);
  not not_10 (not_10_out, e);
  not not_11 (not_11_out, b);
  and and_1 (and_1_out, not_1_out, not_2_out, d);
  and and_2 (and_2_out, not_3_out, d, not_4_out);
  and and_3 (and_3_out, not_5_out, c, not_6_out);
  and and_4 (and_4_out, b, not_7_out);
  and and_5 (and_5_out, not_8_out, b, c);
  and and_6 (and_6_out, a, not_9_out, not_10_out);
  and and_7 (and_7_out, a, not_11_out, d);
  or or_1 (x, and_1_out, and_2_out, and_3_out, and_4_out, and_5_out, and_6_out, and_7_out);
endmodule

// FRAG
module ALL___1 (
  input  in_1,
  input  in_2,
  input  in_3,
  input  in_4,
  input  in_5,
  output out_6,
  output out_7,
  output out_8,
  output out_9,
  output out_10,
  output out_11,
  output out_12
);

  _0_A u_0_a_1 (.a(in_1), .b(in_2), .c(in_3), .d(in_4), .e(in_5), .x(out_6));
  _1_B u_1_b_1 (.a(in_1), .b(in_2), .c(in_3), .d(in_4), .e(in_5), .x(out_7));
  _2_C u_2_c_1 (.a(in_1), .b(in_2), .c(in_3), .d(in_4), .e(in_5), .x(out_8));
  _3_D u_3_d_1 (.a(in_1), .b(in_2), .c(in_3), .d(in_4), .e(in_5), .x(out_9));
  _4_E u_4_e_1 (.a(in_1), .b(in_2), .c(in_3), .d(in_4), .e(in_5), .x(out_10));
  _5_F u_5_f_1 (.a(in_1), .b(in_2), .c(in_3), .d(in_4), .e(in_5), .x(out_11));
  _6_G u_6_g_1 (.a(in_1), .b(in_2), .c(in_3), .d(in_4), .e(in_5), .x(out_12));
endmodule

// FRAG
module ALL___2 (
  input  in_1,
  input  in_2,
  input  in_3,
  input  in_4,
  input  in_5,
  output out_6,
  output out_7,
  output out_8,
  output out_9,
  output out_10,
  output out_11,
  output out_12
);

  _0__a u_0_a_1 (.a(in_1), .b(in_2), .c(in_3), .d(in_4), .e(in_5), .x(out_6));
  _1__b u_1_b_1 (.a(in_1), .b(in_2), .c(in_3), .d(in_4), .e(in_5), .x(out_7));
  _2__c u_2_c_1 (.a(in_1), .b(in_2), .c(in_3), .d(in_4), .e(in_5), .x(out_8));
  _3__d u_3_d_1 (.a(in_1), .b(in_2), .c(in_3), .d(in_4), .e(in_5), .x(out_9));
  _4__e u_4_e_1 (.a(in_1), .b(in_2), .c(in_3), .d(in_4), .e(in_5), .x(out_10));
  _5__f u_5_f_1 (.a(in_1), .b(in_2), .c(in_3), .d(in_4), .e(in_5), .x(out_11));
  _6__g u_6_g_1 (.a(in_1), .b(in_2), .c(in_3), .d(in_4), .e(in_5), .x(out_12));
endmodule

// PRIMOS
module N__PRIMOS (
  input  a,
  input  b,
  input  c,
  input  d,
  input  e,
  output x
);

  wire and_1_out, and_2_out, and_3_out, and_4_out, and_5_out, and_6_out, not_1_out, not_2_out, not_3_out,
       not_4_out, not_5_out, not_6_out, not_7_out, not_8_out, not_9_out, not_10_out;

  not not_1 (not_1_out, a);
  not not_2 (not_2_out, b);
  not not_3 (not_3_out, b);
  not not_4 (not_4_out, c);
  not not_5 (not_5_out, a);
  not not_6 (not_6_out, b);
  not not_7 (not_7_out, c);
  not not_8 (not_8_out, a);
  not not_9 (not_9_out, c);
  not not_10 (not_10_out, d);
  and and_1 (and_1_out, not_1_out, not_2_out, e);
  and and_2 (and_2_out, not_3_out, not_4_out, e);
  and and_3 (and_3_out, not_5_out, not_6_out, not_7_out, d);
  and and_4 (and_4_out, not_8_out, not_9_out, d, e);
  and and_5 (and_5_out, b, c, not_10_out, e);
  and and_6 (and_6_out, a, c, d, e);
  or or_1 (x, and_1_out, and_2_out, and_3_out, and_4_out, and_5_out, and_6_out);
endmodule

module N_7_SEGMENTS (
  input  A,
  input  B,
  input  C,
  input  D,
  input  E
);

  wire _1_out_6, _1_out_7, _1_out_8, _1_out_9, _1_out_10, _1_out_11, _1_out_12, all_2_1_out_6, all_2_1_out_7,
       all_2_1_out_8, all_2_1_out_9, all_2_1_out_10, all_2_1_out_11, all_2_1_out_12, n_primos_1_x;

  LED led_1 (.in(n_primos_1_x));
  N__PRIMOS n_primos_1 (.a(A), .b(B), .c(C), .d(D), .e(E), .x(n_primos_1_x));
  ALL___1 _1 (
    .in_1(A), .in_2(B), .in_3(C), .in_4(D), .in_5(E), .out_6(_1_out_6), .out_7(_1_out_7), .out_8(_1_out_8),
    .out_9(_1_out_9), .out_10(_1_out_10), .out_11(_1_out_11), .out_12(_1_out_12));
  ALL___2 all_2_1 (
    .in_1(A), .in_2(B), .in_3(C), .in_4(D), .in_5(E), .out_6(all_2_1_out_6), .out_7(all_2_1_out_7),
    .out_8(all_2_1_out_8), .out_9(all_2_1_out_9), .out_10(all_2_1_out_10), .out_11(all_2_1_out_11),
    .out_12(all_2_1_out_12));
  _7_Segment_Display u_7_segment_display_1 (
    .g(_1_out_12), .f(_1_out_11), .a(_1_out_6), .b(_1_out_7), .e(_1_out_10), .d(_1_out_9), .c(_1_out_8));  // open: dp
  _7_Segment_Display u_7_segment_display_2 (
    .g(all_2_1_out_12), .f(all_2_1_out_11), .a(all_2_1_out_6), .b(all_2_1_out_7), .e(all_2_1_out_10),
    .d(all_2_1_out_9), .c(all_2_1_out_8));  // open: dp

  // Notes on the sheet:
  //    número primo
  //   1
  //   2
endmodule
